# Fritzing sketch zapojeni (saved by Fritzing 1.0.6)
breadboards: 1

parts:
  M2 = DC Motor [voltage_(max)=12V voltage_(min)=3V part_number=Větráček]
  Micro_bit = Microbit [part_number="breakout board"]
  V1 = DC Power Supply [voltage=12V internal_resistance=1Ω max_current=2A part_number=Zdroj]
  A1 = L298N DC motor driver [part_number=H-můstek]
  HC-SR04_Sensor_1 = HC-SR04 Ultrasonic Distance Sensor [part_number=Sonar]

nets:
  N1: M2.pin_1, A1.OUT2
  N2: M2.pin_2, A1.OUT1
  N3: Micro_bit.P1, A1.IN1
  N4: Micro_bit.P2, HC-SR04_Sensor_1.TRIG, HC-SR04_Sensor_1.ECHO
  3V3: Micro_bit.3V3, HC-SR04_Sensor_1.VCC
  GND: Micro_bit.GND, V1.Pin_1, A1.GND, A1.IN2, HC-SR04_Sensor_1.GND
  N5: V1.Pin_2, A1.12V, A1.5V-ENA-JMP-I, A1.5V-ENA-JMP-O
  N6: A1.+5V-J1, A1.ENA

custom parts:
  Microbit: BBC Microbit Fritzing part. May 2019 expanded to include schematic and pcb views as well as breadboard. PCB view assumes an Adafruit PRODUCT ID: 3342 2x40 Right Angle through hole edge connector (although others will probably work as well). The pcb svg is custom (see forum article http://forum.fritzing.org/t/making-edge-connectors-and-both-side-smd-parts/7287 for an explaination if you need to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
  L298N DC motor driver: This L298N Motor Driver Module is a high power motor driver module for driving DC and Stepper Motors. This module consists of an L298 motor driver IC and a 78M05 5V regulator.
